// Logisim project LedGame.circ as structural Verilog: 1 circuit, main circuit main
module main (
);

  wire and_1_out, and_2_out, and_3_out, and_4_out, and_5_out, and_6_out, and_7_out, and_8_out, and_9_out,
       and_10_out, and_11_out, and_12_out, and_13_out, and_14_out, and_15_out, and_16_out, and_17_out,
       and_18_out, and_19_out, and_20_out, B1_out, B2_out, clock_1_out, or_1_out, or_2_out, or_3_out, R_out,
       S1_q, S1_qn, S2_q, S3_q;

  Button B1 (.out(B1_out));
  Button B2 (.out(B2_out));
  Button R (.out(R_out));
  and and_1 (and_1_out, B1_out, ~B2_out, ~R_out);  // AND_Gate
  and and_2 (and_2_out, ~B1_out, B2_out, ~R_out);  // AND_Gate
  and and_3 (and_3_out, ~B1_out, ~B2_out, R_out);  // AND_Gate
  and and_4 (and_4_out, S3_q, ~S2_q, S1_q, ~and_3_out, ~and_1_out);  // AND_Gate
  Clock clock_1 (.out(clock_1_out));
  or or_1 (or_1_out, and_4_out, and_5_out, and_6_out);
  and and_5 (and_5_out, ~S3_q, S2_q, S1_q, ~and_3_out, ~and_1_out);  // AND_Gate
  and and_6 (and_6_out, ~S3_q, ~S2_q, ~S1_q, ~and_3_out, and_2_out, ~and_1_out);  // AND_Gate
  D_Flip_Flop S1 (.clk(clock_1_out), .D(or_1_out), .Q(S1_q), .Qn(S1_qn));  // open: preset, en, reset
  and and_7 (and_7_out, ~S1_q, S2_q, S3_q);  // AND_Gate
  and and_8 (and_8_out, ~S1_q, S2_q, ~S3_q);  // AND_Gate
  and and_9 (and_9_out, ~S1_q, ~S2_q, S3_q);  // AND_Gate
  and and_10 (and_10_out, ~S1_q, ~S2_q, ~S3_q);  // AND_Gate
  and and_11 (and_11_out, S1_q, S2_q, ~S3_q);  // AND_Gate
  and and_12 (and_12_out, S1_q, ~S2_q, S3_q);  // AND_Gate
  and and_13 (and_13_out, S1_q, ~S2_q, ~S3_q);  // AND_Gate
  D_Flip_Flop S2 (.clk(clock_1_out), .D(or_2_out), .Q(S2_q));  // open: Qn, preset, en, reset
  and and_14 (and_14_out, ~S3_q, S2_q, ~S1_q, ~and_3_out, ~and_2_out);  // AND_Gate
  D_Flip_Flop S3 (.clk(clock_1_out), .D(or_3_out), .Q(S3_q));  // open: Qn, preset, en, reset
  or or_2 (or_2_out, and_14_out, and_15_out, and_16_out, and_17_out);
  and and_15 (and_15_out, ~S3_q, S2_q, ~and_3_out, ~and_2_out, ~and_1_out);  // AND_Gate
  and and_16 (and_16_out, ~S3_q, ~S2_q, ~S1_q, ~and_3_out, and_2_out, ~and_1_out);  // AND_Gate
  and and_17 (and_17_out, S3_q, ~S2_q, ~S1_q, ~and_3_out, ~and_2_out, and_1_out);  // AND_Gate
  LED Led0 (.in(and_7_out));
  LED Led1 (.in(and_8_out));
  LED Led2 (.in(and_9_out));
  LED Led3 (.in(and_10_out));
  LED Led4 (.in(and_11_out));
  LED Led5 (.in(and_12_out));
  LED Led6 (.in(and_13_out));
  and and_18 (and_18_out, S3_q, ~S2_q, ~and_3_out, ~and_2_out, ~and_1_out);  // AND_Gate
  or or_3 (or_3_out, and_18_out, and_19_out, and_20_out);
  and and_19 (and_19_out, ~S3_q, S2_q, ~and_3_out, and_2_out, ~and_1_out);  // AND_Gate
  and and_20 (and_20_out, ~S3_q, ~S1_q, ~and_3_out, ~and_2_out, and_1_out);  // AND_Gate
endmodule
