// Logisim project 16bit_multiplier.circ as structural Verilog: 1 circuit, main circuit main
module main (
  input  go,
  input  [15:0] a_in,
  input  [15:0] b_in,
  output [15:0] Result,
  output [2:0] state
);

  wire clock_1_out, main_1_la, main_1_lb, main_1_lmult, main_1_lres, main_1_sa, main_1_sr, main_2_eq,
       main_2_gt;

  Clock clock_1 (.out(clock_1_out));
  FSM_main main_1 (
    .gt(main_2_gt), .eq(main_2_eq), .go(go), .CLK(clock_1_out), .La(main_1_la), .Lb(main_1_lb),
    .Lmult(main_1_lmult), .Lres(main_1_lres), .Sa(main_1_sa), .Sr(main_1_sr), .state(state));
  datapath_main main_2 (
    .Sa(main_1_sa), .a_in(a_in), .La(main_1_la), .b_in(b_in), .Lb(main_1_lb), .CLK(clock_1_out),
    .Lmult(main_1_lmult), .Sr(main_1_sr), .Lres(main_1_lres), .gt(main_2_gt), .res(Result), .eq(main_2_eq));
endmodule
