// Logisim project FSM.circ as structural Verilog: 1 circuit, main circuit main
module main (
  input  gt,
  input  eq,
  input  go,
  input  CLK,
  output La,
  output Lb,
  output Lmult,
  output Lres,
  output Sa,
  output Sr,
  output [2:0] state
);

  wire and_1_out, and_2_out, and_3_out, and_4_out, and_6_out, and_7_out;
  wire [2:0] or_1_out;

  or or_1 (or_1_out[0], and_1_out, and_2_out);
  and and_1 (and_1_out, ~eq, gt, ~state[0], state[1], ~state[2]);  // AND_Gate
  and and_2 (and_2_out, go, ~state[0], ~state[1], ~state[2]);  // AND_Gate
  or or_2 (or_1_out[1], and_3_out, and_4_out);
  and and_3 (and_3_out, state[0], ~state[2]);  // AND_Gate
  and and_4 (and_4_out, ~eq, gt, ~state[0], state[1], ~state[2]);  // AND_Gate
  Register #(.width(3)) stateReg (.D(or_1_out), .Q(state), .clk(CLK));  // open: en, clr
  and and_5 (or_1_out[2], eq, ~gt, ~state[0], state[1], ~state[2]);  // AND_Gate
  and and_6 (and_6_out, state[0], state[1], ~state[2]);  // AND_Gate
  and and_7 (and_7_out, ~state[0], ~state[1], ~state[2]);  // AND_Gate
  and and_8 (La, state[0], ~state[2]);  // AND_Gate
  and and_9 (Lb, state[0], ~state[1], ~state[2]);  // AND_Gate
  or or_3 (Lmult, and_6_out, and_7_out);
  and and_10 (Lres, ~state[0], ~state[1]);  // AND_Gate
  and and_11 (Sa, state[0], state[1], ~state[2]);  // AND_Gate
  and and_12 (Sr, ~state[0], ~state[1], ~state[2]);  // AND_Gate
endmodule
