// Logisim project datapath.circ as structural Verilog: 1 circuit, main circuit main
module main (
  input  Sa,
  input  [15:0] a_in,
  input  La,
  input  [15:0] b_in,
  input  Lb,
  input  CLK,
  input  Lres,
  input  Lmult,
  input  Sr,
  output gt,
  output [15:0] res,
  output eq
);

  wire [15:0] a_q, adder_1_out, b_q, mult_q, multiplexer_1_out, multiplexer_2_out, multiplexer_3_out,
       subtractor_1_out;

  Multiplexer #(.width(16), .enable("false")) multiplexer_1 (
    .in0(a_in), .in1(subtractor_1_out), .out(multiplexer_1_out), .sel(Sa));
  Register #(.width(16)) a (.D(multiplexer_1_out), .en(La), .Q(a_q), .clk(CLK));  // open: clr
  Register #(.width(16)) b (.D(b_in), .en(Lb), .Q(b_q), .clk(CLK));  // open: clr
  Subtractor #(.width(16)) subtractor_1 (.a(a_q), .b(16'h1), .out(subtractor_1_out), .bin(1'b0));  // open: bout
  Adder #(.width(16)) adder_1 (.a(b_q), .b(mult_q), .out(adder_1_out));  // open: cin, cout
  Comparator #(.width(16)) comparator_1 (.a(a_q), .b({16{1'b0}}), .gt(gt), .eq(eq));  // open: lt
  Multiplexer #(.width(16), .enable("false")) multiplexer_2 (
    .in0(adder_1_out), .in1({16{1'b0}}), .out(multiplexer_2_out), .sel(Sr));
  Register #(.width(16)) mult (.D(multiplexer_2_out), .en(Lmult), .Q(mult_q), .clk(CLK));  // open: clr
  Multiplexer #(.width(16), .enable("false")) multiplexer_3 (
    .in0(mult_q), .in1({16{1'b0}}), .out(multiplexer_3_out), .sel(Sr));
  Register #(.width(16)) u_res (.D(multiplexer_3_out), .en(Lres), .Q(res), .clk(CLK));  // open: clr
endmodule
